// Digital circuit main.dig as structural Verilog
module main (
  input  in_1,
  input  [31:0] PC,
  input  in_3,
  input  Clock,
  input  [31:0] Write_back,
  input  Write_enable
);

  wire [4:0] multiplexer_1_out;
  wire [31:0] instruction_mem_1__32b__out;

  instruction_mem instruction_mem_1 (._32b__ADDR(PC), ._1b__Enable(in_3), ._32b__Out(instruction_mem_1__32b__out));
  Multiplexer #(.Bits(5)) multiplexer_1 (
    .sel(in_1), .in_0(instruction_mem_1__32b__out[20:16]), .in_1(instruction_mem_1__32b__out[15:11]),
    .out(multiplexer_1_out));
  _32x32 _32x32_1 (
    ._32_W_d(Write_back), ._5__R_reg1(instruction_mem_1__32b__out[25:21]),
    ._5__R_reg2(instruction_mem_1__32b__out[20:16]), ._5b__A_set(multiplexer_1_out), .Clk(Clock),
    ._1__W_e(Write_enable));  // open: R_d1, R_d2, R31
  ula ula_1 ();  // open: ALUControl, A, B, Shamt, Zero, Resultado
  extensao_de_sinal_1_32 extensao_de_sinal_1_32_1 ();  // open: A, S

  // Other names for the same wires on the sheet: Reg_dest = in_1
endmodule
